// Logisim project 4winsLED.circ as structural Verilog: 4 circuits, main circuit main
module main (
);

  wire and_1_out, and_2_out, button_1_out, button_2_out, or_1_out, Reset_out, sr_flipflop_1_q,
       sr_flipflop_2_q, sr_flipflop_3_q, sr_flipflop_4_q;

  SR_Flipflop sr_flipflop_1 (.R(Reset_out), .S(button_1_out), .Q(sr_flipflop_1_q));  // open: minus_Q
  SR_Flipflop sr_flipflop_2 (.R(Reset_out), .S(button_2_out), .Q(sr_flipflop_2_q));  // open: minus_Q
  Button Reset (.out(Reset_out));
  and and_1 (and_1_out, sr_flipflop_2_q, or_1_out);
  and and_2 (and_2_out, sr_flipflop_1_q, or_1_out);
  or or_1 (or_1_out, sr_flipflop_3_q, sr_flipflop_4_q);
  SR_Flipflop sr_flipflop_3 (.R(Reset_out), .S(button_2_out), .Q(sr_flipflop_3_q));  // open: minus_Q
  SR_Flipflop sr_flipflop_4 (.R(Reset_out), .S(button_1_out), .Q(sr_flipflop_4_q));  // open: minus_Q
  Button button_1 (.out(button_1_out));
  Button button_2 (.out(button_2_out));
  LED led_1 (.in(and_2_out));
  LED led_2 (.in(and_1_out));
  LED led_3 (.in(sr_flipflop_3_q));
  LED led_4 (.in(sr_flipflop_4_q));
endmodule

module _4wins (
);

  Button button_1 ();  // open: out
  DotMatrix #(.matrixcols(7), .matrixrows(6), .dotshape("circle")) dotmatrix_1 ();  // open: col0, col1, col2, col3, col4, col5, col6
  main main_1 ();
endmodule

module SR_Flipflop (
  input  R,
  input  S,
  output Q,
  output minus_Q
);

  nor nor_1 (Q, R, minus_Q);
  nor nor_2 (minus_Q, Q, S);
endmodule

module counter7 (
);

  wire clock_1_out, decoder_1_out0, decoder_1_out1, decoder_1_out2, decoder_1_out3, decoder_1_out4,
       decoder_1_out5, decoder_1_out6, decoder_1_out7;
  wire [2:0] counter_1_q;

  Counter #(.width(3), .max('h7)) counter_1 (.Q(counter_1_q), .clk(clock_1_out));  // open: load, D, count, carry, clr
  Clock clock_1 (.out(clock_1_out));
  Decoder #(.select(3)) decoder_1 (
    .out0(decoder_1_out0), .out1(decoder_1_out1), .out2(decoder_1_out2), .out3(decoder_1_out3),
    .out4(decoder_1_out4), .out5(decoder_1_out5), .out6(decoder_1_out6), .out7(decoder_1_out7),
    .sel(counter_1_q));  // open: en
  LED led_1 (.in(decoder_1_out0));
  LED led_2 (.in(decoder_1_out1));
  LED led_3 (.in(decoder_1_out2));
  LED led_4 (.in(decoder_1_out3));
  LED led_5 (.in(decoder_1_out4));
  LED led_6 (.in(decoder_1_out5));
  LED led_7 (.in(decoder_1_out6));
  LED led_8 (.in(decoder_1_out7));
endmodule
