// Logisim project 8BitAdder.circ as structural Verilog
module FullAdder (
  input  A,
  input  B,
  input  CIN,
  output COUT,
  output S
);

  wire and_1_out, and_2_out, xor_1_out;

  and and_1 (and_1_out, A, B);
  xor xor_1 (xor_1_out, A, B);
  and and_2 (and_2_out, xor_1_out, CIN);
  xor xor_2 (S, xor_1_out, CIN);
  or or_1 (COUT, and_1_out, and_2_out);
endmodule

module _8BitAdder (
  input  A,
  input  B,
  input  CIN
);

  wire fulladder_2_cout, fulladder_3_cout, fulladder_4_cout;

  FullAdder fulladder_1 (.CIN(fulladder_2_cout));  // open: A, B, COUT, S
  FullAdder fulladder_2 (.CIN(fulladder_3_cout), .COUT(fulladder_2_cout));  // open: A, B, S
  FullAdder fulladder_3 (.CIN(fulladder_4_cout), .COUT(fulladder_3_cout));  // open: A, B, S
  FullAdder fulladder_4 (.A(A), .B(B), .CIN(CIN), .COUT(fulladder_4_cout));  // open: S
endmodule
