// Logisim project connect4.circ as structural Verilog: 5 circuits, main circuit main
module main (
  input  in_1,
  input  in_2,
  input  in_3,
  input  in_4,
  input  in_5,
  input  in_6,
  input  [5:0] in_7
);

  wire and_1_out, and_5_out, button_2_out, button_9_out, or_1_out, SRFlipFlop_minus_q, SRFlipFlop_q,
       Start_out;
  wire [5:0] undriven, undriven_2, undriven_3, undriven_4, undriven_5;

  DotMatrix #(.matrixcols(7), .matrixrows(6), .dotshape("circle")) dotmatrix_1 (
    .col0(undriven), .col1(undriven_2), .col3(undriven_3), .col4(undriven_4), .col5(undriven_5), .col6(in_7));  // open: col2
  Button button_1 ();  // open: out
  Button button_2 (.out(button_2_out));
  Button button_3 ();  // open: out
  and and_1 (and_1_out, button_2_out, SRFlipFlop_q);
  // AND_Gate and_2 has open pins: in3=SRFlipFlop_q, out=open
  Button button_4 ();  // open: out
  Button button_5 ();  // open: out
  // AND_Gate and_3 has open pins: in3=SRFlipFlop_q, out=open
  Button button_6 ();  // open: out
  Button button_7 ();  // open: out
  // AND_Gate and_4 has open pins: in3=SRFlipFlop_q, out=open
  Button Start (.out(Start_out));
  or or_1 (or_1_out, Start_out, and_5_out);
  SRFlipFlop SRFlipFlop (.R(and_1_out), .S(or_1_out), .Q(SRFlipFlop_q), .minus_Q(SRFlipFlop_minus_q));
  Button button_8 ();  // open: out
  Button button_9 (.out(button_9_out));
  Button button_10 ();  // open: out
  and and_5 (and_5_out, SRFlipFlop_minus_q, button_9_out);
  // AND_Gate and_6 has open pins: in1=SRFlipFlop_minus_q, out=open
  Button button_11 ();  // open: out
  Button button_12 ();  // open: out
  // AND_Gate and_7 has open pins: in1=SRFlipFlop_minus_q, out=open
  Button button_13 ();  // open: out
  Button button_14 ();  // open: out
  // AND_Gate and_8 has open pins: in1=SRFlipFlop_minus_q, out=open
endmodule

module FullAdder (
  input  A,
  input  B,
  input  Cin,
  output Cout,
  output S
);

  wire and_1_out, and_2_out, xor_1_out;

  and and_1 (and_1_out, A, B);
  xor xor_1 (xor_1_out, A, B);
  and and_2 (and_2_out, xor_1_out, xor_1_out, Cin);
  xor xor_2 (S, xor_1_out, Cin);
  or or_1 (Cout, and_1_out, and_2_out);
endmodule

module SRFlipFlop (
  input  R,
  input  S,
  output Q,
  output minus_Q
);

  nor nor_1 (Q, R, minus_Q);
  nor nor_2 (minus_Q, Q, S);
endmodule

module clock (
  input  in_1,
  output out_2,
  output out_3,
  output out_4,
  output out_5,
  output out_6,
  output out_7,
  output out_8,
  output out_9,
  output out_10,
  output out_11,
  output out_12,
  output out_13,
  output out_14,
  output out_15,
  output out_16,
  output out_17
);

  wire decoder_1_out1, decoder_1_out2, decoder_1_out3, decoder_1_out4, decoder_1_out5, decoder_1_out6,
       decoder_1_out7, decoder_1_out8, decoder_1_out9, decoder_1_out10, decoder_1_out11, decoder_1_out12,
       decoder_1_out13, decoder_1_out14, decoder_1_out15;
  wire [3:0] counter_1_q, not_1_out;

  Counter #(.width(4), .max('he)) counter_1 (.Q(counter_1_q), .clk(in_1));  // open: load, D, count, carry, clr
  // Probe on counter_1_q
  Decoder #(.select(4)) decoder_1 (
    .out0(out_2), .out1(decoder_1_out1), .out2(decoder_1_out2), .out3(decoder_1_out3), .out4(decoder_1_out4),
    .out5(decoder_1_out5), .out6(decoder_1_out6), .out7(decoder_1_out7), .out8(decoder_1_out8),
    .out9(decoder_1_out9), .out10(decoder_1_out10), .out11(decoder_1_out11), .out12(decoder_1_out12),
    .out13(decoder_1_out13), .out14(decoder_1_out14), .out15(decoder_1_out15), .sel(not_1_out));  // open: en
  assign not_1_out = ~counter_1_q;  // NOT_Gate not_1, 4 bits wide
  or or_1 (out_15, out_14, decoder_1_out13);
  or or_2 (out_17, out_16, decoder_1_out15);
  or or_3 (out_3, out_2, decoder_1_out1);
  or or_4 (out_5, out_4, decoder_1_out3);
  or or_5 (out_7, out_6, decoder_1_out5);
  or or_6 (out_9, out_8, decoder_1_out7);
  or or_7 (out_10, out_9, decoder_1_out8);
  or or_8 (out_11, out_10, decoder_1_out9);
  or or_9 (out_13, out_12, decoder_1_out11);
  or or_10 (out_14, out_13, decoder_1_out12);
  or or_11 (out_16, out_15, decoder_1_out14);
  or or_12 (out_4, out_3, decoder_1_out2);
  or or_13 (out_6, out_5, decoder_1_out4);
  or or_14 (out_8, out_7, decoder_1_out6);
  or or_15 (out_12, out_11, decoder_1_out10);
endmodule

module led_filler (
  input  Player_1,
  input  Player_2
);

  wire button_1_out, clock_1_out_3, clock_1_out_4, clock_1_out_5, clock_1_out_6, clock_1_out_7,
       clock_1_out_8, clock_1_out_9, clock_1_out_10, clock_1_out_11, clock_1_out_12, clock_1_out_13,
       clock_1_out_14, clock_1_out_15, clock_1_out_16;

  Button button_1 (.out(button_1_out));
  clock clock_1 (
    .in_1(button_1_out), .out_3(clock_1_out_3), .out_4(clock_1_out_4), .out_5(clock_1_out_5),
    .out_6(clock_1_out_6), .out_7(clock_1_out_7), .out_8(clock_1_out_8), .out_9(clock_1_out_9),
    .out_10(clock_1_out_10), .out_11(clock_1_out_11), .out_12(clock_1_out_12), .out_13(clock_1_out_13),
    .out_14(clock_1_out_14), .out_15(clock_1_out_15), .out_16(clock_1_out_16));  // open: out_2, out_17
  LED led_1 (.in(clock_1_out_4));
  LED led_2 (.in(clock_1_out_6));
  LED led_3 (.in(clock_1_out_8));
  LED led_4 (.in(clock_1_out_10));
  LED led_5 (.in(clock_1_out_12));
  LED led_6 (.in(clock_1_out_14));
  LED led_7 (.in(clock_1_out_16));
  LED led_8 (.in(clock_1_out_3));
  LED led_9 (.in(clock_1_out_5));
  LED led_10 (.in(clock_1_out_7));
  LED led_11 (.in(clock_1_out_9));
  LED led_12 (.in(clock_1_out_11));
  LED led_13 (.in(clock_1_out_13));
  LED led_14 (.in(clock_1_out_15));
endmodule
